# Fritzing sketch arduino_remote_daikin_ethernetshield_ciruit (saved by Fritzing 0.9.2b)
breadboards: 1

parts:
  元件1 = Arduino Uno (Rev3) - ICSP  # not connected
  Q1 = TRANSISTOR_NPN [part_number=2N3904 package=to-92-ammo]
  LED1 = LEDs [package=led10mm]  # not connected
  R1 = Resistor [tolerance=±5% resistance=330 package=THT]
  R2 = Resistor [tolerance=±5% resistance=56 package=THT]
  元件2 = Arduino Ethernet Shield (Rev3)
  DHT1 = DHT11 Humitidy and Temperature Sensor

nets:
  GND: Q1.E, 元件2.GND, DHT1.GND
  N1: Q1.B, R1.Pin_1
  N2: R1.Pin_0, 元件2.PWM_D3
  5V: R2.Pin_1, 元件2.5V, DHT1.VDD
  N3: 元件2.D2, DHT1.DATA

notes:
  電晶體(diode)：2N3904
  紅外線發射(ir)：LIR034
  電阻(resister)：330歐姆
  電阻(resister)：56歐姆
  DHT11

custom parts:
  DHT11 Humitidy and Temperature Sensor: DHT11 Humidity and Temperature Sensor
